# Fritzing sketch 14 LED chaser (saved by Fritzing 0.8.7b)
breadboards: 1

parts:
  U1 = ATmega 328P [package=dip]
  XTAL1 = Crystal [frequency="16 Mhz" package=THT]
  C1 = Capacitor [package=cap-pth-small2]
  C2 = Capacitor [package=cap-pth-small2]  # not connected
  LED1 = LED - 5mm [color="Red (633nm)" package="5 mm [THT]"]
  LED2 = LED - 5mm [color="Red (633nm)" package="5 mm [THT]"]
  LED3 = LED - 5mm [color="Red (633nm)" package="5 mm [THT]"]
  LED4 = LED - 5mm [color="Red (633nm)" package="5 mm [THT]"]
  LED5 = LED - 5mm [color="Red (633nm)" package="5 mm [THT]"]
  LED6 = LED - 5mm [color="Red (633nm)" package="5 mm [THT]"]
  LED7 = LED - 5mm [color="Red (633nm)" package="5 mm [THT]"]
  LED8 = LED - 5mm [color="Red (633nm)" package="5 mm [THT]"]
  LED9 = LED - 5mm [color="Red (633nm)" package="5 mm [THT]"]
  LED10 = LED - 5mm [color="Red (633nm)" package="5 mm [THT]"]
  LED11 = LED - 5mm [color="Red (633nm)" package="5 mm [THT]"]
  LED12 = LED - 5mm [color="Red (633nm)" package="5 mm [THT]"]
  LED13 = LED - 5mm [color="Red (633nm)" package="5 mm [THT]"]
  LED14 = LED - 5mm [color="Red (633nm)" package="5 mm [THT]"]
  VCC1 = 4 x AAA Battery Mount
  R1 = Resistor [tolerance=±5% resistance=220 package=THT]
  R2 = Resistor [tolerance=±5% resistance=220 package=THT]
  R3 = Resistor [tolerance=±5% resistance=220 package=THT]
  R4 = Resistor [tolerance=±5% resistance=220 package=THT]
  R5 = Resistor [tolerance=±5% resistance=220 package=THT]
  R6 = Resistor [tolerance=±5% resistance=220 package=THT]
  R7 = Resistor [tolerance=±5% resistance=220 package=THT]
  R8 = Resistor [tolerance=±5% resistance=220 package=THT]
  R9 = Resistor [tolerance=±5% resistance=220 package=THT]
  R10 = Resistor [tolerance=±5% resistance=220 package=THT]
  R11 = Resistor [tolerance=±5% resistance=220 package=THT]
  R12 = Resistor [tolerance=±5% resistance=220 package=THT]
  R13 = Resistor [tolerance=±5% resistance=220 package=THT]
  R14 = Resistor [tolerance=±5% resistance=220 package=THT]

nets:
  N1: U1.PD0_(PCINT16/RXD)_[D0], R1.Pin_0
  N2: U1.PD1_(PCINT17/TXD)_[D1], R2.Pin_0
  N3: U1.PD2_(PCINT18/INT0)_[D2], R3.Pin_0
  N4: U1.PD3_(PCINT19/OC2B/INT1)_[D3_PWM], R4.Pin_0
  N5: U1.PD4_(PCINT20/XCK/T0)_[D4], R5.Pin_0
  N6: U1.VCC, U1.AVCC, VCC1.+
  GND: U1.GND, C1.2, VCC1.-
  N7: U1.PB6_(PCINT6/XTAL1/TOSC1)_[XTAL1], XTAL1.pin_0
  N8: U1.PB7_(PCINT7/XTAL2/TOSC2)_[XTAL2], XTAL1.pin_1
  N9: U1.PD5_(PCINT21/OC0B/T1)_[D5_PWM], R6.Pin_0
  N10: U1.PD6_(PCINT22/OC0A/AIN0)_[D6_PWM], R7.Pin_0
  N11: U1.PD7_(PCINT23/AIN1)_[D7], R8.Pin_0
  N12: U1.PB0_(PCINT0/CLK0/ICP1)_[D8], R9.Pin_0
  N13: U1.PB1_(OC1A/PCINT1)_[D9_PWM], R10.Pin_0
  N14: U1.PB2_(^SS/OC1B/PCINT2)_[D10_PWM], R11.Pin_0
  N15: U1.PB3_(MOSI/OC2A/PCINT3)_[D11_PWM], R12.Pin_0
  N16: U1.PB4_(MISO/PCINT4)_[D12], R13.Pin_0
  N17: U1.PB5_(SCK/PCINT5)_[D13], R14.Pin_0
  N18: LED1.cathode, LED14.cathode
  N19: LED1.anode, R1.Pin_1
  N20: LED2.anode, R2.Pin_1
  N21: LED3.anode, R3.Pin_1
  N22: LED4.anode, R4.Pin_1
  N23: LED5.anode, R8.Pin_1
  N24: LED6.anode, R5.Pin_1
  N25: LED7.anode, R6.Pin_1
  N26: LED8.anode, R7.Pin_1
  N27: LED9.anode, R9.Pin_1
  N28: LED10.anode, R10.Pin_1
  N29: LED11.anode, R11.Pin_1
  N30: LED12.anode, R12.Pin_1
  N31: LED13.anode, R13.Pin_1
  N32: LED14.anode, R14.Pin_1

custom parts:
  ATmega 328P: Atmel ATmega 328P-PU Microcontroller
